# Fritzing sketch DRV8834_accel_stepper (saved by Fritzing 1.0.3b)
breadboards: 1

parts:
  Part1 = Adafruit ESP32-S2 TFT Feather [part_number="Adafruit #5300"]
  Pololu_A1 = Pololu A4988 [package=SO16]
  M1 = Stepper Motor - Bipolar
  VCC1 = 4 x AAA Battery Mount [internal_resistance=0.1Ω]
  C1 = Electrolytic Capacitor [capacitance=1µF voltage=35V package="100 mil [THT, electrolytic]"]

nets:
  N1: Part1.GND, Pololu_A1.GND#8
  N2: Part1.3.3V, Pololu_A1.SLEEP
  N3: Part1.D6, Pololu_A1.DIR
  N4: Part1.D5, Pololu_A1.STEP
  N5: Pololu_A1.1B, M1.D
  N6: Pololu_A1.1A, M1.B
  N7: Pololu_A1.2A, M1.C
  N8: Pololu_A1.2B, M1.A
  N9: Pololu_A1.GND#14, VCC1.-, C1.-
  N10: Pololu_A1.VMOT, VCC1.+, C1.+

notes:
  5 STEP
  6 DIR

custom parts:
  Adafruit ESP32-S2 TFT Feather: We've got a new machine here at Adafruit, it can uncover your deepest desires. Don't believe me? I'll turn it on right now to prove it to you! What, you want unlimited mozzarella sticks? OK well, that's not something we can provide. But we can provide your second-deepest desire: an ESP32-S2 Feather board with a built in IPS TFT color display. It's got all the gooeyness of a mozzarella stick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
