# Fritzing sketch dc_motor_transistor_tip122 (saved by Fritzing 1.0.3b)
breadboards: 1

parts:
  Q1 = TIP120 Hi-Current Darlington Transistor
  Part1 = Adafruit ESP32-S2 TFT Feather [part_number="Adafruit #5300"]
  M1 = gear-motor
  R1 = Resistor [tolerance=±5% power=0.25W resistance=1k package=THT]
  VCC1 = 4 x AAA Battery Mount [internal_resistance=0.1Ω]

nets:
  N1: Q1.BASE, R1.Pin_1
  N2: Q1.COLLECTOR, M1.pin_2
  N3: Q1.EMITTER, Part1.GND, VCC1.-
  N4: Part1.D5, R1.Pin_0
  N5: M1.pin_1, VCC1.+

notes:
  B C E

custom parts:
  Adafruit ESP32-S2 TFT Feather: We've got a new machine here at Adafruit, it can uncover your deepest desires. Don't believe me? I'll turn it on right now to prove it to you! What, you want unlimited mozzarella sticks? OK well, that's not something we can provide. But we can provide your second-deepest desire: an ESP32-S2 Feather board with a built in IPS TFT color display. It's got all the gooeyness of a mozzarella stick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
