# Fritzing sketch hc_sr04_distance (saved by Fritzing 1.0.3b)
breadboards: 1

parts:
  Part1 = Adafruit ESP32-S2 TFT Feather [part_number="Adafruit #5300"]
  HC-SR04_Sensor_1 = HC-SR04 Ultrasonic Distance Sensor
  U1 = Voltage Regulator - 5V [package="TO220 [THT]"]
  J1 = Basic Servo  # not connected

nets:
  GND: Part1.GND, HC-SR04_Sensor_1.GND, U1.input_voltage
  3.3V: Part1.3.3V, HC-SR04_Sensor_1.VCC
  N1: Part1.D6, HC-SR04_Sensor_1.ECHO
  N2: Part1.D5, HC-SR04_Sensor_1.TRIG

notes:
  VOUT
  VIN
  GND
  5
  6

custom parts:
  Adafruit ESP32-S2 TFT Feather: We've got a new machine here at Adafruit, it can uncover your deepest desires. Don't believe me? I'll turn it on right now to prove it to you! What, you want unlimited mozzarella sticks? OK well, that's not something we can provide. But we can provide your second-deepest desire: an ESP32-S2 Feather board with a built in IPS TFT color display. It's got all the gooeyness of a mozzarella stick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
