# Fritzing sketch neopixel_demo (saved by Fritzing 1.0.2b)
breadboards: 1

parts:
  Part1 = Adafruit ESP32-S3 TFT Feather [part_number="Adafruit #5483"]
  NEOPIXEL1 = Neopixel Strip -- Black (60/m) [part_number=1461]

nets:
  GND: Part1.GND, NEOPIXEL1.GND
  3.3V: Part1.3.3V, NEOPIXEL1.+5V
  N1: Part1.D5, NEOPIXEL1.DI

custom parts:
  Adafruit ESP32-S3 TFT Feather: We've got a new machine here at Adafruit, it can uncover your deepest desires. Don't believe me? I'll turn it on right now to prove it to you! What, you want your very own soft serve ice cream machine? OK well, that's not something we can provide. But we can provide your second-deepest desire: an ESP32-S3 Feather board with a built in IPS TFT color display. It's got all the delicious creamy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
  Neopixel Strip -- Black (60/m): Neopixel Strip, Black, 60 pixels per meter.
