# Fritzing sketch web_control_servo (saved by Fritzing 1.0.3b)
breadboards: 1

parts:
  Part1 = Adafruit ESP32-S2 TFT Feather [part_number="Adafruit #5300"]
  J1 = Basic Servo

nets:
  GND: Part1.GND, J1.gnd
  N1: Part1.VBUS, J1.vcc
  N2: Part1.D12, J1.pulse

custom parts:
  Adafruit ESP32-S2 TFT Feather: We've got a new machine here at Adafruit, it can uncover your deepest desires. Don't believe me? I'll turn it on right now to prove it to you! What, you want unlimited mozzarella sticks? OK well, that's not something we can provide. But we can provide your second-deepest desire: an ESP32-S2 Feather board with a built in IPS TFT color display. It's got all the gooeyness of a mozzarella stick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
